# Fritzing sketch Ejercicio21 (saved by Fritzing 0.9.2b)
breadboards: 1

parts:
  Parte1 = Arduino Uno (Rev3)
  IC1 = L293D [package=THT]
  M1 = DC Motor
  S1 = Pushbutton [package="[THT]"]
  S2 = Pushbutton [package="[THT]"]
  R1 = Resistor [tolerance=±5% resistance=220 package="0805 [SMD]"]
  R2 = Resistor [tolerance=±5% resistance=220 package="0805 [SMD]"]
  R3 = Rotary Potentiometer (Small) [maximum_resistance=100kΩ package=THT]
  VCC1 = Battery block 9V

nets:
  N1: Parte1.A0, R3.wiper
  N2: Parte1.D9_PWM, IC1.Enable_1
  N3: Parte1.GND, IC1.0V, R1.Pin_1, R2.Pin_1, R3.leg1, R3.leg2, VCC1.-
  N4: Parte1.D2, IC1.In_2
  N5: Parte1.D3_PWM, IC1.In_1
  N6: Parte1.D4, S2.Pin_1, S2.Pin_2, R2.Pin_0
  N7: Parte1.D5_PWM, S1.Pin_1, S1.Pin_2, R1.Pin_0
  N8: Parte1.5V, IC1.+V, S1.Pin_3, S1.Pin_4, S2.Pin_3, S2.Pin_4
  N9: IC1.Out_1_(_Controlled_by_Enable_1_), M1.pin_1
  N10: IC1.Out_2_(_Controlled_by_Enable_1_), M1.pin_2
  N11: IC1.+Vmotor, VCC1.+
